# Fritzing sketch Temp_Tracker (saved by Fritzing 0.9.1b)
breadboards: 1

parts:
  R1 = Resistor [tolerance=±5% resistance=4.7k package=THT]
  DS1 = DS18B20 1-Wire Temperature Sensor [part_number=DS18B20]
  Raspberry_Pi1 = Raspberry Pi B+

nets:
  N1: R1.Pin_0, Raspberry_Pi1.3v3
  N2: R1.Pin_1, DS1.DQ, Raspberry_Pi1.GPIO4, Raspberry_Pi1.GPIO24
  GND: DS1.GND, Raspberry_Pi1.GND
